// Digital circuit computah.dig as structural Verilog
module computah (
  input  clk
);

  wire d, demultiplexer_1_out_0, demultiplexer_1_out_1, demultiplexer_1_out_2, demultiplexer_1_out_3,
       demultiplexer_1_out_4, demultiplexer_1_out_5, demultiplexer_1_out_6, demultiplexer_1_out_7,
       demultiplexer_1_out_8, demultiplexer_1_out_9, demultiplexer_1_out_10, demultiplexer_1_out_11,
       demultiplexer_1_out_12, demultiplexer_1_out_13, demultiplexer_1_out_14, demultiplexer_1_out_15, m_oe,
       m_we;
  wire [3:0] sel;
  wire [11:0] addr;

  ROM rom_1 (.D(d));  // open: A, sel
  // main main_1: pin names not known; wires that end beside it: d, clk, {sel, addr}, m_we, m_oe
  // Or or_1 has open pins: In_1=demultiplexer_1_out_8, In_2=demultiplexer_1_out_9, In_3=demultiplexer_1_out_10, In_4=demultiplexer_1_out_11, In_5=demultiplexer_1_out_12, In_6=demultiplexer_1_out_13, In_7=demultiplexer_1_out_14, In_8=demultiplexer_1_out_15, out=open
  // Or or_2 has open pins: In_1=demultiplexer_1_out_0, In_2=demultiplexer_1_out_1, In_3=demultiplexer_1_out_2, In_4=demultiplexer_1_out_3, In_5=demultiplexer_1_out_4, In_6=demultiplexer_1_out_5, In_7=demultiplexer_1_out_6, In_8=demultiplexer_1_out_7, out=open
  Demultiplexer #(.Selector_Bits(4)) demultiplexer_1 (
    .sel(sel), .in(m_we), .out_0(demultiplexer_1_out_0), .out_1(demultiplexer_1_out_1),
    .out_2(demultiplexer_1_out_2), .out_3(demultiplexer_1_out_3), .out_4(demultiplexer_1_out_4),
    .out_5(demultiplexer_1_out_5), .out_6(demultiplexer_1_out_6), .out_7(demultiplexer_1_out_7),
    .out_8(demultiplexer_1_out_8), .out_9(demultiplexer_1_out_9), .out_10(demultiplexer_1_out_10),
    .out_11(demultiplexer_1_out_11), .out_12(demultiplexer_1_out_12), .out_13(demultiplexer_1_out_13),
    .out_14(demultiplexer_1_out_14), .out_15(demultiplexer_1_out_15));
  Demultiplexer #(.Selector_Bits(4)) demultiplexer_2 (
    .sel(sel), .in(m_oe));  // open: out_0, out_1, out_2, out_3, out_4, out_5, out_6, out_7, out_8, out_9, out_10, out_11, out_12, out_13, out_14, out_15

  // Other names for the same wires on the sheet: c = clk
endmodule
