// Digital circuit main.dig as structural Verilog
module main (
  input  [7:0] D_in,
  input  C,
  output [15:0] A_bus,
  output m_we,
  output m_oe
);

  wire and_1_out, bus_transceiver_1_p1, carry, clk_x, clk_y, cond, cond_upc_clr, dst_a, dst_b, dst_x, dst_y,
       f_c, f_z, flags_we, ir0_rd, ir1_rd, multiplexer_1_out, not_1_out, not_2_out, not_3_out, or_1_out,
       or_2_out, pc_inc, pc_rd, pc_src, src_a, src_addr, src_alu, src_b, src_external, src_imm8, src_shr,
       src_x, src_y, upc_clr, Y_ovf, zero;
  wire [1:0] alu_op, uPC_out;
  wire [2:0] dst_data;
  wire [3:0] src_data;
  wire [3:2] op;
  wire [7:0] a_cont, alu_1_s, b_cont, bus_transceiver_1_p3, imm8, register_1_q, register_2_q;
  wire [7:4] rom_3_d;
  wire [11:0] imm12;
  wire [15:0] driver_1_out, pc_content, XY;

  not not_1 (not_1_out, src_addr);
  and and_1 (and_1_out, not_2_out, cond_upc_clr);
  not not_2 (not_2_out, cond);
  or or_1 (or_1_out, and_1_out, upc_clr);
  or or_2 (or_2_out, pc_rd, pc_inc);
  assign driver_1_out = pc_src ? XY : 16'bz;  // Driver driver_1
  assign driver_1_out = not_3_out ? {pc_content[15:12], imm12} : 16'bz;  // Driver driver_2
  Counter #(.Bits(2)) uPC (.en(1'b1), .C(C), .clr(or_1_out), .out(uPC_out));  // open: ovf
  ROM #(.AddrBits(6), .Bits(8)) rom_1 (.A({op, alu_op, uPC_out}), .sel(1'b1), .D({m_oe, dst_data, src_data}));
  not not_3 (not_3_out, pc_src);
  ROM #(.AddrBits(6), .Bits(8)) rom_2 (
    .A({op, alu_op, uPC_out}), .sel(1'b1), .D({clk_x, ir1_rd, ir0_rd, pc_src, pc_rd, pc_inc, src_addr, m_we}));
  CounterPreset #(.Bits(16)) PC (
    .en(or_2_out), .C(C), .dir(1'b0), .in(driver_1_out), .ld(pc_rd), .clr(1'b0), .out(pc_content));  // open: ovf
  Decoder #(.Selector_Bits(4)) decoder_1 (
    .sel(src_data), .out_1(src_a), .out_2(src_b), .out_3(src_x), .out_4(src_y), .out_5(src_alu),
    .out_6(src_shr), .out_7(src_imm8), .out_8(src_external));  // open: out_0, out_9, out_10, out_11, out_12, out_13, out_14, out_15
  assign A_bus = not_1_out ? pc_content : 16'bz;  // Driver driver_3
  ROM #(.AddrBits(6), .Bits(8)) rom_3 (
    .A({op, alu_op, uPC_out}), .sel(1'b1), .D({rom_3_d, cond_upc_clr, upc_clr, flags_we, clk_y}));
  assign A_bus = src_addr ? XY : 16'bz;  // Driver driver_4
  Decoder #(.Selector_Bits(3)) decoder_2 (
    .sel(dst_data), .out_1(dst_a), .out_2(dst_b), .out_3(dst_x), .out_4(dst_y));  // open: out_0, out_5, out_6, out_7
  decoder decoder_3 (.b0(register_2_q), .b1(register_1_q), .op({op, alu_op}), .imm_12(imm12), .imm_8(imm8));
  Register #(.Bits(8)) register_1 (.D(bus_transceiver_1_p3), .C(C), .en(ir1_rd), .Q(register_1_q));
  Register #(.Bits(8)) register_2 (.D(bus_transceiver_1_p3), .C(C), .en(ir0_rd), .Q(register_2_q));
  // bus_transceiver bus_transceiver_1: pin names not known; wires that end beside it: bus_transceiver_1_p1, 1'b0, bus_transceiver_1_p3, D_in
  not not_4 (bus_transceiver_1_p1, src_external);
  assign bus_transceiver_1_p3 = src_a ? a_cont : 8'bz;  // Driver driver_5
  assign bus_transceiver_1_p3 = src_b ? b_cont : 8'bz;  // Driver driver_6
  assign bus_transceiver_1_p3 = src_x ? XY[15:8] : 8'bz;  // Driver driver_7
  assign bus_transceiver_1_p3 = src_y ? XY[7:0] : 8'bz;  // Driver driver_8
  assign bus_transceiver_1_p3 = src_imm8 ? imm8 : 8'bz;  // Driver driver_9
  Register #(.Bits(8)) A (.D(bus_transceiver_1_p3), .C(C), .en(dst_a), .Q(a_cont));
  Register #(.Bits(8)) B (.D(bus_transceiver_1_p3), .C(C), .en(dst_b), .Q(b_cont));
  CounterPreset #(.Bits(8)) X (
    .en(Y_ovf), .C(C), .dir(1'b0), .in(bus_transceiver_1_p3), .ld(dst_x), .clr(1'b0), .out(XY[15:8]));  // open: ovf
  CounterPreset #(.Bits(8)) Y (
    .en(clk_y), .C(C), .dir(1'b0), .in(bus_transceiver_1_p3), .ld(dst_y), .clr(1'b0), .out(XY[7:0]),
    .ovf(Y_ovf));
  assign bus_transceiver_1_p3 = src_alu ? alu_1_s : 8'bz;  // Driver driver_10
  assign bus_transceiver_1_p3 = src_shr ? {1'b0, a_cont[7:1]} : 8'bz;  // Driver driver_11
  Multiplexer multiplexer_1 (.sel(src_shr), .in_0(carry), .in_1(a_cont[0]), .out(multiplexer_1_out));
  Multiplexer multiplexer_2 (.sel(alu_op[0]), .in_0(f_z), .in_1(f_c), .out(cond));
  alu alu_1 (.b(b_cont), .a(a_cont), .op(alu_op), .s(alu_1_s), .c(carry), .z(zero));
  D_FF d_ff_1 (.D(zero), .C(flags_we), .Q(f_z));  // open: nQ
  D_FF d_ff_2 (.D(multiplexer_1_out), .C(flags_we), .Q(f_c));  // open: nQ

  // Other names for the same wires on the sheet: mem_oe = m_oe; mem_we = m_we; shr_c = a_cont[0]; op[1:0] = alu_op

  // Notes on the sheet:
  //   C: Hz: 10
  //   PC & Address Bus
  //   Microcode
  //   contents of rom_1 (hex, n*v repeats v):
  //   88,88,15,0,88,88,15,0,88,88,15,0,88,88,15,0,88,98,0,0,88,88,31
  //   ,0,88,88,41,0,88,88,98,0,88,88,1,0,88,88,21,0,88,88,16,0,88,88
  //   ,0,0,88,88,0,0,88,88,0,0,88,88,0,0,88,88
  //   contents of rom_2 (hex, n*v repeats v):
  //   24,44,0,0,24,44,0,0,24,44,0,0,24,44,0,0,24,44,0,0,24,44,0,0,24
  //   ,44,0,0,24,44,2,0,24,44,3,0,24,44,0,0,24,44,0,0,24,44,80,0,24
  //   ,44,8,0,24,44,18,0,24,44,0,8,24,44,0,8
  //   contents of rom_3 (hex, n*v repeats v):
  //   0,0,6,0,0,0,6,0,0,0,6,0,0,0,6,0,0,0,4,0,0,0,4,0,0,0,4,0,0,0,4
  //   ,0,0,0,4,0,0,0,4,0,0,0,6,0,0,0,5,0,0,0,4,0,0,0,4,0,0,0,8,4,0,0
  //   ,8,4
  //   IRs
  //   Registers
  //   ALU & Shift
  //   Flags
endmodule
